# Fritzing sketch Sketsa MiniProject 6 RFID (saved by Fritzing 0.9.3b)
breadboards: 1

parts:
  U1 = ESP32S-HiLetgo [part_number=ESP32S-HiLetgo]
  Part2 = RFID-RC522 [part_number=101218]

nets:
  N1: U1.3.3, Part2.3.3V
  GND: U1.GND, Part2.GND
  N2: U1.GPIO18, Part2.SCK
  N3: U1.GPIO19, Part2.MISO
  N4: U1.GPIO21, Part2.SDA
  N5: U1.GPIO22, Part2.RST
  N6: U1.GPIO23, Part2.MOSI

custom parts:
  ESP32S-HiLetgo: HiLetgo ESP-WROOM-32 ESP32 ESP-32S Development Board 2.4GHz Dual-Mode WiFi + Bluetooth Dual Cores Microcontroller The ESP32 integrated with Antenna switches, RF Balun, power amplifiers, low-noise amplifiers, filters, and management modules, and the entire solution occupies the least area of PCB. 2.4 GHz Wi-Fi plus Bluetooth dual-mode chip, with TSMC Ultra-low power consumption 40nm technology,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
